// Logisim project 7segmentfinal.circ as structural Verilog: 8 circuits, main circuit main
module main (
  input  S,
  input  T,
  input  U,
  input  V
);

  wire A_out_5, B_out_5, C_out_5, D_out_5, E_out_5, F_out_5, G_out_5;

  B B (.S(S), .T(T), .U(U), .V(V), .out_5(B_out_5));
  A A (.S(S), .T(T), .U(U), .V(V), .out_5(A_out_5));
  F F (.S(S), .T(T), .U(U), .V(V), .out_5(F_out_5));
  G G (.S(S), .T(T), .U(U), .V(V), .out_5(G_out_5));
  E E (.S(S), .T(T), .U(U), .V(V), .out_5(E_out_5));
  D D (.S(S), .T(T), .U(U), .V(V), .out_5(D_out_5));
  C C (.S(S), .T(T), .U(U), .V(V), .out_5(C_out_5));
  _7_Segment_Display u_7_segment_display_1 (
    .g(G_out_5), .f(F_out_5), .a(A_out_5), .b(B_out_5), .e(E_out_5), .d(D_out_5), .c(C_out_5));  // open: dp
endmodule

module A (
  input  S,
  input  T,
  input  U,
  input  V,
  output out_5
);

  wire and_1_out, and_2_out, and_3_out, and_4_out, and_5_out, and_6_out, not_1_out, not_2_out, not_3_out,
       not_4_out;

  not not_1 (not_1_out, S);
  not not_2 (not_2_out, U);
  not not_3 (not_3_out, T);
  not not_4 (not_4_out, V);
  and and_1 (and_1_out, not_3_out, not_4_out);
  and and_2 (and_2_out, not_1_out, U);
  and and_3 (and_3_out, T, U);
  and and_4 (and_4_out, S, not_4_out);
  and and_5 (and_5_out, not_1_out, T, V);
  and and_6 (and_6_out, S, not_3_out, not_2_out);
  or or_1 (out_5, and_1_out, and_2_out, and_3_out, and_4_out, and_5_out, and_6_out);
endmodule

module B (
  input  S,
  input  T,
  input  U,
  input  V,
  output out_5
);

  wire and_1_out, and_2_out, and_3_out, and_4_out, and_5_out, nand_1_out, nand_2_out, nand_3_out, nand_4_out;

  nand nand_1 (nand_1_out, S, S);
  nand nand_2 (nand_2_out, T, T);
  nand nand_3 (nand_3_out, V, V);
  nand nand_4 (nand_4_out, U, U);
  and and_1 (and_1_out, nand_1_out, nand_2_out);
  and and_2 (and_2_out, nand_2_out, nand_3_out);
  and and_3 (and_3_out, nand_1_out, nand_4_out, nand_3_out);
  and and_4 (and_4_out, nand_1_out, U, V);
  and and_5 (and_5_out, S, nand_4_out, V);
  or or_1 (out_5, and_1_out, and_2_out, and_3_out, and_4_out, and_5_out);
endmodule

module C (
  input  S,
  input  T,
  input  U,
  input  V,
  output out_5
);

  wire and_1_out, and_2_out, and_3_out, and_4_out, and_5_out, nand_1_out, nand_2_out, nand_3_out, nand_4_out;

  nand nand_1 (nand_1_out, S, S);
  nand nand_2 (nand_2_out, T, T);
  nand nand_3 (nand_3_out, V, V);
  nand nand_4 (nand_4_out, U, U);
  and and_1 (and_1_out, nand_4_out, V);
  and and_2 (and_2_out, S, nand_2_out);
  and and_3 (and_3_out, nand_1_out, T);
  and and_4 (and_4_out, nand_1_out, V);
  and and_5 (and_5_out, nand_1_out, nand_4_out);
  or or_1 (out_5, and_1_out, and_2_out, and_3_out, and_4_out, and_5_out);
endmodule

module D (
  input  S,
  input  T,
  input  U,
  input  V,
  output out_5
);

  wire and_1_out, and_2_out, and_3_out, and_4_out, and_5_out, nand_1_out, nand_2_out, nand_3_out, nand_4_out;

  nand nand_1 (nand_1_out, S, S);
  nand nand_2 (nand_2_out, T, T);
  nand nand_3 (nand_3_out, U, U);
  nand nand_4 (nand_4_out, V, V);
  and and_1 (and_1_out, nand_1_out, nand_2_out, nand_4_out);
  and and_2 (and_2_out, nand_2_out, U, V);
  and and_3 (and_3_out, T, nand_3_out, V);
  and and_4 (and_4_out, T, U, nand_4_out);
  and and_5 (and_5_out, S, nand_3_out, nand_4_out);
  or or_1 (out_5, and_1_out, and_2_out, and_3_out, and_4_out, and_5_out);
endmodule

module E (
  input  S,
  input  T,
  input  U,
  input  V,
  output out_5
);

  wire and_1_out, and_2_out, and_3_out, and_4_out, nand_1_out, nand_2_out, nand_3_out, nand_4_out;

  nand nand_1 (nand_1_out, S, S);
  nand nand_2 (nand_2_out, T, T);
  nand nand_3 (nand_3_out, U, U);
  nand nand_4 (nand_4_out, V, V);
  and and_1 (and_1_out, nand_2_out, nand_4_out);
  and and_2 (and_2_out, U, nand_4_out);
  and and_3 (and_3_out, S, T);
  and and_4 (and_4_out, S, U);
  or or_1 (out_5, and_1_out, and_2_out, and_3_out, and_4_out);
endmodule

module F (
  input  S,
  input  T,
  input  U,
  input  V,
  output out_5
);

  wire and_1_out, and_2_out, and_3_out, and_4_out, and_5_out, nand_1_out, nand_2_out, nand_3_out, nand_4_out;

  nand nand_1 (nand_1_out, S, S);
  nand nand_2 (nand_2_out, T, T);
  nand nand_3 (nand_3_out, V, V);
  nand nand_4 (nand_4_out, U, U);
  and and_1 (and_1_out, nand_4_out, nand_3_out);
  and and_2 (and_2_out, T, nand_3_out);
  and and_3 (and_3_out, S, nand_2_out);
  and and_4 (and_4_out, S, U);
  and and_5 (and_5_out, nand_1_out, T, nand_4_out);
  or or_1 (out_5, and_1_out, and_2_out, and_3_out, and_4_out, and_5_out);
endmodule

module G (
  input  S,
  input  T,
  input  U,
  input  V,
  output out_5
);

  wire and_1_out, and_2_out, and_3_out, and_4_out, and_5_out, nand_1_out, nand_2_out, nand_3_out, nand_4_out;

  nand nand_1 (nand_1_out, S, S);
  nand nand_2 (nand_2_out, T, T);
  nand nand_3 (nand_3_out, U, U);
  nand nand_4 (nand_4_out, V, V);
  and and_1 (and_1_out, nand_2_out, U);
  and and_2 (and_2_out, U, nand_4_out);
  and and_3 (and_3_out, S, nand_2_out);
  and and_4 (and_4_out, S, V);
  and and_5 (and_5_out, nand_1_out, T, nand_3_out);
  or or_1 (out_5, and_1_out, and_2_out, and_3_out, and_4_out, and_5_out);
endmodule
