// Logisim project Opptil31.circ as structural Verilog: 1 circuit, main circuit main
module main (
  input  in_1,
  input  in_2,
  input  in_3,
  input  in_4,
  input  in_5,
  input  in_6
);

  wire A_out, B_out, C_out, D_out, decoder_1_out0, decoder_1_out1, decoder_1_out2, decoder_1_out3,
       decoder_1_out4, decoder_1_out5, decoder_1_out6, decoder_1_out7, decoder_1_out8, decoder_1_out9,
       decoder_1_out10, decoder_1_out11, decoder_1_out12, decoder_1_out13, decoder_1_out14, decoder_1_out15,
       decoder_1_out16, decoder_1_out17, decoder_1_out18, decoder_1_out19, decoder_1_out20, decoder_1_out21,
       decoder_1_out22, decoder_1_out23, decoder_1_out24, decoder_1_out25, decoder_1_out26, decoder_1_out27,
       decoder_1_out28, decoder_1_out29, decoder_1_out30, decoder_1_out31, E_out, F_out, G_out, H_out, J_out,
       K_out, L_out, M_out, N_out;

  Decoder #(.select(5)) decoder_1 (
    .out0(decoder_1_out0), .out1(decoder_1_out1), .out2(decoder_1_out2), .out3(decoder_1_out3),
    .out4(decoder_1_out4), .out5(decoder_1_out5), .out6(decoder_1_out6), .out7(decoder_1_out7),
    .out8(decoder_1_out8), .out9(decoder_1_out9), .out10(decoder_1_out10), .out11(decoder_1_out11),
    .out12(decoder_1_out12), .out13(decoder_1_out13), .out14(decoder_1_out14), .out15(decoder_1_out15),
    .out16(decoder_1_out16), .out17(decoder_1_out17), .out18(decoder_1_out18), .out19(decoder_1_out19),
    .out20(decoder_1_out20), .out21(decoder_1_out21), .out22(decoder_1_out22), .out23(decoder_1_out23),
    .out24(decoder_1_out24), .out25(decoder_1_out25), .out26(decoder_1_out26), .out27(decoder_1_out27),
    .out28(decoder_1_out28), .out29(decoder_1_out29), .out30(decoder_1_out30), .out31(decoder_1_out31),
    .sel({in_1, in_2, in_3, in_4, in_5}));  // open: en
  nor H (H_out, decoder_1_out10, decoder_1_out11, decoder_1_out12, decoder_1_out13, decoder_1_out14, decoder_1_out15, decoder_1_out16, decoder_1_out17, decoder_1_out18, decoder_1_out19);
  nor J (J_out, decoder_1_out20, decoder_1_out21, decoder_1_out22, decoder_1_out23, decoder_1_out24, decoder_1_out25, decoder_1_out26, decoder_1_out27, decoder_1_out28, decoder_1_out29);
  nor K (K_out, decoder_1_out10, decoder_1_out11, decoder_1_out12, decoder_1_out13, decoder_1_out14, decoder_1_out15, decoder_1_out16, decoder_1_out17, decoder_1_out18, decoder_1_out19);
  nor L (L_out, decoder_1_out10, decoder_1_out11, decoder_1_out12, decoder_1_out13, decoder_1_out14, decoder_1_out15, decoder_1_out16, decoder_1_out17, decoder_1_out18, decoder_1_out19, decoder_1_out30, decoder_1_out31);
  or M (M_out, decoder_1_out0, decoder_1_out1, decoder_1_out2, decoder_1_out3, decoder_1_out4, decoder_1_out5, decoder_1_out6, decoder_1_out7, decoder_1_out8, decoder_1_out9);
  or N (N_out, decoder_1_out20, decoder_1_out21, decoder_1_out22, decoder_1_out23, decoder_1_out24, decoder_1_out25, decoder_1_out26, decoder_1_out27, decoder_1_out28, decoder_1_out29, decoder_1_out30, decoder_1_out31);
  _7_Segment_Display u_7_segment_display_1 (
    .g(N_out), .f(M_out), .a(H_out), .b(in_6), .e(L_out), .d(K_out), .c(J_out));  // open: dp
  _7_Segment_Display u_7_segment_display_2 (
    .g(G_out), .f(F_out), .a(A_out), .b(B_out), .e(E_out), .d(D_out), .c(C_out));  // open: dp
  nor A (A_out, decoder_1_out1, decoder_1_out4, decoder_1_out11, decoder_1_out14, decoder_1_out21, decoder_1_out24, decoder_1_out31);
  nor B (B_out, decoder_1_out5, decoder_1_out6, decoder_1_out15, decoder_1_out16, decoder_1_out25, decoder_1_out26);
  nor C (C_out, decoder_1_out2, decoder_1_out12, decoder_1_out22);
  nor D (D_out, decoder_1_out1, decoder_1_out4, decoder_1_out7, decoder_1_out9, decoder_1_out11, decoder_1_out14, decoder_1_out17, decoder_1_out19, decoder_1_out21, decoder_1_out24, decoder_1_out27, decoder_1_out29, decoder_1_out31);
  or E (E_out, decoder_1_out0, decoder_1_out2, decoder_1_out6, decoder_1_out8, decoder_1_out10, decoder_1_out12, decoder_1_out16, decoder_1_out18, decoder_1_out20, decoder_1_out22, decoder_1_out26, decoder_1_out28, decoder_1_out30);
  NotExactlyOne F (
    .out(F_out), .in0(decoder_1_out1), .in1(decoder_1_out2), .in2(decoder_1_out3), .in3(decoder_1_out7),
    .in4(decoder_1_out11), .in5(decoder_1_out12), .in6(decoder_1_out13), .in7(decoder_1_out17),
    .in8(decoder_1_out21), .in9(decoder_1_out22), .in10(decoder_1_out23), .in11(decoder_1_out27),
    .in12(decoder_1_out31));
  nor G (G_out, decoder_1_out0, decoder_1_out1, decoder_1_out7, decoder_1_out10, decoder_1_out11, decoder_1_out17, decoder_1_out20, decoder_1_out21, decoder_1_out27, decoder_1_out30, decoder_1_out31);
endmodule
