// Logisim project oblig1vers2.circ as structural Verilog: 4 circuits, main circuit main
module main (
  input  in_1,
  input  X3,
  input  X2,
  input  X1,
  input  X0,
  output _256,
  output _128,
  output _64,
  output _32,
  output _16,
  output _8,
  output _4,
  output _2,
  output _1
);

  hoved hoved_1 (
    .X3(X3), .X2(X2), .X1(X1), .X0(X0), .Negative(in_1), ._1(_1), ._2(_2), ._4(_4), ._8(_8), ._16(_16),
    ._32(_32), ._64(_64), ._128(_128), ._256(_256));

  // Notes on the sheet:
  //   multiply by +10 : 0
  //   Multiply by -10 : 1
endmodule

module Halfadder (
  input  A,
  input  B,
  output Cout,
  output S
);

  and and_1 (Cout, A, B);
  xor xor_1 (S, A, B);
endmodule

module Fulladder (
  input  Cin,
  input  B,
  input  A,
  output out_4,
  output S
);

  wire and_1_out, and_2_out, xor_1_out;

  and and_1 (and_1_out, A, B);
  or or_1 (out_4, and_1_out, and_2_out);
  and and_2 (and_2_out, Cin, xor_1_out);
  xor xor_1 (xor_1_out, B, A);
  xor xor_2 (S, Cin, xor_1_out);
endmodule

module hoved (
  input  X3,
  input  X2,
  input  X1,
  input  X0,
  input  Negative,
  output _1,
  output _2,
  output _4,
  output _8,
  output _16,
  output _32,
  output _64,
  output _128,
  output _256
);

  wire fulladder_1_out_4, fulladder_1_s, halfadder_1_cout, halfadder_1_s, halfadder_2_cout, halfadder_2_s,
       halfadder_3_cout, halfadder_3_s, halfadder_4_cout, halfadder_5_cout, halfadder_6_cout,
       halfadder_7_cout, halfadder_8_cout, halfadder_9_cout, halfadder_10_cout, halfadder_11_cout, xor_1_out,
       xor_2_out, xor_3_out, xor_4_out, xor_5_out, xor_6_out, xor_7_out;

  Halfadder halfadder_1 (.A(X2), .B(X0), .Cout(halfadder_1_cout), .S(halfadder_1_s));
  Fulladder fulladder_1 (.Cin(halfadder_1_cout), .B(X3), .A(X1), .out_4(fulladder_1_out_4), .S(fulladder_1_s));
  Halfadder halfadder_2 (.A(X2), .B(fulladder_1_out_4), .Cout(halfadder_2_cout), .S(halfadder_2_s));
  Halfadder halfadder_3 (.A(X3), .B(halfadder_2_cout), .Cout(halfadder_3_cout), .S(halfadder_3_s));
  Halfadder halfadder_4 (.A(Negative), .B(Negative), .Cout(halfadder_4_cout), .S(_1));
  Halfadder halfadder_5 (.A(xor_1_out), .B(halfadder_4_cout), .Cout(halfadder_5_cout), .S(_2));
  xor xor_1 (xor_1_out, Negative, X0);
  Halfadder halfadder_6 (.A(xor_2_out), .B(halfadder_5_cout), .Cout(halfadder_6_cout), .S(_4));
  xor xor_2 (xor_2_out, Negative, X1);
  xor xor_3 (xor_3_out, Negative, halfadder_1_s);
  Halfadder halfadder_7 (.A(xor_3_out), .B(halfadder_6_cout), .Cout(halfadder_7_cout), .S(_8));
  Halfadder halfadder_8 (.A(xor_4_out), .B(halfadder_7_cout), .Cout(halfadder_8_cout), .S(_16));
  xor xor_4 (xor_4_out, Negative, fulladder_1_s);
  Halfadder halfadder_9 (.A(xor_5_out), .B(halfadder_8_cout), .Cout(halfadder_9_cout), .S(_32));
  xor xor_5 (xor_5_out, Negative, halfadder_2_s);
  Halfadder halfadder_10 (.A(xor_6_out), .B(halfadder_9_cout), .Cout(halfadder_10_cout), .S(_64));
  xor xor_6 (xor_6_out, Negative, halfadder_3_s);
  Halfadder halfadder_11 (.A(xor_7_out), .B(halfadder_10_cout), .Cout(halfadder_11_cout), .S(_128));
  xor xor_7 (xor_7_out, Negative, halfadder_3_cout);
  xor xor_8 (_256, halfadder_11_cout, Negative);
endmodule
