// Logisim project Oblig2.circ as structural Verilog: 4 circuits, main circuit main
module main (
);

  wire Clk, LoadR, LSB, MSB, Reset, WriteR;
  wire [3:0] _4BitOut, counter_1_out_2;
  wire [7:0] databuss, DataFromRAM, ram_1_data, ReadData;

  Clock clock_1 (.out(Clk));
  Button button_1 (.out(Reset));
  counter counter_1 (.out_2(counter_1_out_2), .Clear(Reset));
  Decoder decoder_1 (.in_1(ram_1_data), .LSB(LSB), .MSB(MSB), .LoadR(LoadR), .WriteR(WriteR), .out_6(_4BitOut));
  RAM #(.addrWidth(4)) ram_1 (.addr(counter_1_out_2), .data(ram_1_data), .clk(Clk));  // open: sel, ld, clr
  Logic logic_1 (
    ._4BitOut(_4BitOut), .Lsb(LSB), .Msb(MSB), .WriteR(WriteR), .in_5(Reset), .in_6(DataFromRAM),
    .Buss(databuss), .OutputToReg(ReadData));
  RAM #(.addrWidth(4), .bus("separate")) ram_2 (
    .addr(_4BitOut), .din(ReadData), .data(DataFromRAM), .str(WriteR), .clk(Clk), .ld(LoadR), .clr(Reset));  // open: sel

  // Notes on the sheet:
  //   Program
  //   Data
endmodule

module counter (
  input  Clear,
  output [3:0] out_2
);

  wire and_1_out, clk_out, not_1_out;
  wire [3:0] adder_1_out;

  Adder #(.width(4)) adder_1 (.a(out_2), .b(4'b0001), .out(adder_1_out));  // open: cin, cout
  not not_1 (not_1_out, and_1_out);
  Register #(.width(4)) register_1 (.D(adder_1_out), .en(not_1_out), .Q(out_2), .clk(clk_out), .clr(Clear));
  Clock clk (.out(clk_out));
  and and_1 (and_1_out, out_2[0], out_2[1], out_2[2], out_2[3]);

  // Notes on the sheet:
  //   Adder
  //   Register
endmodule

module Decoder (
  input  [7:0] in_1,
  output LSB,
  output MSB,
  output LoadR,
  output WriteR,
  output [3:0] out_6
);

  wire decoder_1_p1;

  // Decoder_part #(.select(4), .enable("false")) decoder_1: pin names not known; wires that end beside it: decoder_1_p1, decoder_1_p1, in_1[7:4], LSB, MSB, LoadR, WriteR

  assign out_6 = in_1[3:0];
endmodule

module Logic (
  input  [3:0] _4BitOut,
  input  Lsb,
  input  Msb,
  input  WriteR,
  input  in_5,
  input  [7:0] in_6,
  output [7:0] Buss,
  output [7:0] OutputToReg
);

  wire Clk;
  wire [1:0] or_1_out;
  wire [7:0] NewLsb, NewMsb, NewValue;

  Clock clock_1 (.out(Clk));
  assign NewLsb = Lsb ? {Buss[7:4], _4BitOut} : 8'bz;  // Controlled_Buffer controlled_buffer_1
  assign NewMsb = Msb ? {_4BitOut, Buss[3:0]} : 8'bz;  // Controlled_Buffer controlled_buffer_2
  Register register_1 (.D(NewValue), .Q(Buss), .clk(Clk), .clr(in_5));  // open: en
  or or_1 (or_1_out[0], Lsb, WriteR);
  or or_2 (or_1_out[1], WriteR, Msb);
  Multiplexer #(.select(2), .width(8)) multiplexer_1 (
    .in0(in_6), .in1(NewLsb), .in2(NewMsb), .in3(Buss), .out(NewValue), .sel(or_1_out));  // open: en

  assign OutputToReg = Buss;

  // Other names for the same wires on the sheet: DataFromRAM[7:0] = in_6; ResetIn = in_5

  // Notes on the sheet:
  //   DataFromRAM
  //   Hvis WriteR er enablet, skal NewValue være det samme den var
endmodule
